# Fritzing sketch lamp (saved by Fritzing 1.0.1rc)
breadboards: 1

parts:
  Lamp_LEDs = JST-VHR-3N [part_number=JST-VHR-3N package=THT]
  Switch_2 = JST-VHR-3N [part_number=JST-VHR-3N package=THT]
  switch_1 = JST-VHR-3N [part_number=JST-VHR-3N package=THT]
  DC_In_5V = JST-VHR-3N [part_number=JST-VHR-3N package=THT]
  ESP32_DEV = mystery part, 30 pins [chip_label=?]
  Relay_(not_accurate) = WeMos D1 Mini Relay Shield
  Magnifier_LEDs = JST-VHR-3N [part_number=JST-VHR-3N package=THT]
  MOSFET = Basic FET N-Channel [package="TO220 [THT]"]
  V1 = DC Power [voltage=5]
  V2 = DC Power [voltage=3.3V]

nets:
  N1: Lamp_LEDs.pin1, Lamp_LEDs.pin_4, MOSFET.drain
  N2: Lamp_LEDs.pin_6, DC_In_5V.pin_6, ESP32_DEV.pin15, Relay_(not_accurate).5V, Magnifier_LEDs.pin_6
  N3: Switch_2.pin2, Switch_2.pin_5, switch_1.pin2, switch_1.pin_5, ESP32_DEV.pin16, V2.V+
  N4: Switch_2.pin_6, ESP32_DEV.pin11
  N5: switch_1.pin_6, ESP32_DEV.pin12
  GND: DC_In_5V.pin2, DC_In_5V.pin_5, ESP32_DEV.pin14, ESP32_DEV.pin17, Relay_(not_accurate).COM, Relay_(not_accurate).G, MOSFET.source, V1.V-, V2.V-
  N6: ESP32_DEV.pin18, MOSFET.gate
  N7: ESP32_DEV.pin23, Relay_(not_accurate).A0
  N8: Relay_(not_accurate).NO, Magnifier_LEDs.pin_4
